// Logisim project 171044046.circ as structural Verilog: 1 circuit, main circuit main
module main (
);

  wire and_1_out, and_2_out, and_3_out, and_4_out, and_5_out, and_6_out, and_7_out, and_8_out, and_9_out,
       and_10_out, and_11_out, and_12_out, and_13_out, and_14_out, and_15_out, and_16_out, and_17_out,
       and_18_out, and_19_out, and_20_out, and_21_out, and_22_out, and_23_out, and_24_out, and_25_out,
       and_26_out, and_27_out, and_28_out, and_29_out, and_30_out, B1_out, B2_out, button_1_out,
       button_2_out, clock_1_out, or_1_out, or_2_out, or_3_out, or_4_out, or_5_out, RESET_out, S0_out,
       S1_out, S2_out, S3_out, S4_out, S5_out, S6_out, S7_out, S8_out, S9_out, S10_out, S11_out;
  wire [3:0] counter_1_q, counter_2_q, n0_out, register_1_q;

  Button RESET (.out(RESET_out));
  and S9 (S9_out, register_1_q[3], ~register_1_q[2], ~register_1_q[1], register_1_q[0]);  // AND_Gate
  and S11 (S11_out, register_1_q[3], ~register_1_q[2], register_1_q[1], register_1_q[0]);  // AND_Gate
  and S10 (S10_out, register_1_q[3], ~register_1_q[2], register_1_q[1], ~register_1_q[0]);  // AND_Gate
  or or_1 (or_1_out, S9_out, S10_out);
  LED L1 (.in(S11_out));
  Register #(.width(4)) register_1 (.D(n0_out), .en(1'b1), .Q(register_1_q), .clk(clock_1_out), .clr(RESET_out));
  Clock clock_1 (.out(clock_1_out));
  and S8 (S8_out, register_1_q[3], ~register_1_q[2], ~register_1_q[1], ~register_1_q[0]);  // AND_Gate
  and S7 (S7_out, ~register_1_q[3], register_1_q[2], register_1_q[1], register_1_q[0]);  // AND_Gate
  or or_2 (or_2_out, S7_out, S8_out);
  LED L2 (.in(or_1_out));
  LED L3 (.in(or_2_out));
  and S0 (S0_out, ~register_1_q[3], ~register_1_q[2], ~register_1_q[1], ~register_1_q[0]);  // AND_Gate
  or or_3 (or_3_out, S0_out, S1_out);
  LED L4 (.in(or_3_out));
  Button B1 (.out(B1_out));
  Button B2 (.out(B2_out));
  and S2 (S2_out, ~register_1_q[3], ~register_1_q[2], ~register_1_q[1], register_1_q[0]);  // AND_Gate
  and S1 (S1_out, ~register_1_q[3], ~register_1_q[2], ~register_1_q[1], ~register_1_q[0]);  // AND_Gate
  or or_4 (or_4_out, S2_out, S3_out);
  LED L5 (.in(or_4_out));
  and S4 (S4_out, ~register_1_q[3], register_1_q[2], ~register_1_q[1], ~register_1_q[0]);  // AND_Gate
  and S3 (S3_out, ~register_1_q[3], ~register_1_q[2], register_1_q[1], register_1_q[0]);  // AND_Gate
  LED L7 (.in(S6_out));
  LED L6 (.in(or_5_out));
  or or_5 (or_5_out, S4_out, S5_out);
  and S5 (S5_out, ~register_1_q[3], register_1_q[2], ~register_1_q[2], register_1_q[0]);  // AND_Gate
  and S6 (S6_out, ~register_1_q[3], register_1_q[2], register_1_q[1], ~register_1_q[0]);  // AND_Gate
  and and_1 (and_1_out, register_1_q[3], ~register_1_q[2], ~B1_out);  // AND_Gate
  and and_2 (and_2_out, register_1_q[3], ~register_1_q[2], B2_out);  // AND_Gate
  and and_3 (and_3_out, register_1_q[3], ~register_1_q[2], register_1_q[0]);  // AND_Gate
  and and_4 (and_4_out, ~register_1_q[3], register_1_q[2], register_1_q[1], register_1_q[0], ~B1_out, ~B2_out);  // AND_Gate
  and and_5 (and_5_out, ~register_1_q[3], register_1_q[2], ~register_1_q[0]);  // AND_Gate
  and and_6 (and_6_out, ~register_1_q[3], register_1_q[2], B1_out);  // AND_Gate
  and and_7 (and_7_out, ~register_1_q[3], register_1_q[2], ~register_1_q[1], ~B2_out);  // AND_Gate
  and and_8 (and_8_out, ~register_1_q[3], register_1_q[2], register_1_q[1], B2_out);  // AND_Gate
  and and_9 (and_9_out, ~register_1_q[3], ~register_1_q[1], ~register_1_q[0], ~B1_out, B2_out);  // AND_Gate
  and and_10 (and_10_out, ~register_1_q[3], register_1_q[1], register_1_q[0], B1_out, ~B2_out);  // AND_Gate
  and and_11 (and_11_out, register_1_q[3], ~register_1_q[2], register_1_q[1], ~register_1_q[0], B1_out, ~B2_out);  // AND_Gate
  and and_12 (and_12_out, ~register_1_q[3], register_1_q[1], ~register_1_q[0]);  // AND_Gate
  and and_13 (and_13_out, register_1_q[3], ~register_1_q[2], register_1_q[1]);  // AND_Gate
  and and_14 (and_14_out, ~register_1_q[2], register_1_q[1], ~B1_out, ~B2_out);  // AND_Gate
  and and_15 (and_15_out, ~register_1_q[3], register_1_q[1], B1_out, B2_out);  // AND_Gate
  and and_16 (and_16_out, ~register_1_q[3], ~register_1_q[2], ~register_1_q[0], ~B1_out, B2_out);  // AND_Gate
  and and_17 (and_17_out, ~register_1_q[3], ~register_1_q[2], ~register_1_q[0], B1_out, ~B2_out);  // AND_Gate
  and and_18 (and_18_out, ~register_1_q[3], register_1_q[2], register_1_q[0], ~B1_out, B2_out);  // AND_Gate
  and and_19 (and_19_out, ~register_1_q[3], register_1_q[2], register_1_q[0], B1_out, ~B2_out);  // AND_Gate
  and and_20 (and_20_out, register_1_q[3], ~register_1_q[2], register_1_q[0], ~B1_out, ~B2_out);  // AND_Gate
  and and_21 (and_21_out, register_1_q[3], ~register_1_q[2], register_1_q[1], register_1_q[0]);  // AND_Gate
  and and_22 (and_22_out, register_1_q[3], ~register_1_q[2], ~B1_out, B2_out);  // AND_Gate
  and and_23 (and_23_out, register_1_q[3], ~register_1_q[2], B1_out, ~B2_out);  // AND_Gate
  and and_24 (and_24_out, ~register_1_q[3], register_1_q[1], register_1_q[0], B2_out);  // AND_Gate
  and and_25 (and_25_out, ~register_1_q[2], ~register_1_q[1], register_1_q[0], B1_out);  // AND_Gate
  and and_26 (and_26_out, ~register_1_q[2], ~register_1_q[1], ~B1_out, B2_out);  // AND_Gate
  and and_27 (and_27_out, ~register_1_q[3], register_1_q[0], B1_out, B2_out);  // AND_Gate
  and and_28 (and_28_out, ~register_1_q[3], register_1_q[2], register_1_q[1], register_1_q[0], B1_out);  // AND_Gate
  and and_29 (and_29_out, ~register_1_q[3], register_1_q[2], ~register_1_q[1], ~B1_out, ~B2_out);  // AND_Gate
  and and_30 (and_30_out, ~register_1_q[3], ~register_1_q[2], register_1_q[1], ~B1_out, ~B2_out);  // AND_Gate
  Button button_1 (.out(button_1_out));
  Hex_Digit_Display hex_digit_display_1 (.value(counter_1_q));  // open: dp
  Counter #(.width(4), .max('hf)) counter_1 (
    .count(S11_out), .Q(counter_1_q), .clk(S11_out), .clr(button_1_out));  // open: load, D, carry
  Counter #(.width(4), .max('hf)) counter_2 (
    .count(S6_out), .Q(counter_2_q), .clk(S6_out), .clr(button_2_out));  // open: load, D, carry
  Button button_2 (.out(button_2_out));
  or n3 (n0_out[3], and_1_out, and_2_out, and_3_out, and_4_out);
  or n2 (n0_out[2], and_5_out, and_6_out, and_7_out, and_8_out, and_9_out, and_10_out, and_11_out);
  or n1 (n0_out[1], and_12_out, and_13_out, and_14_out, and_15_out, and_16_out, and_17_out, and_18_out, and_19_out, and_20_out);
  or n0 (n0_out[0], and_21_out, and_22_out, and_23_out, and_24_out, and_25_out, and_26_out, and_27_out, and_28_out, and_29_out, and_30_out);
  Hex_Digit_Display hex_digit_display_2 (.value(counter_2_q));  // open: dp

  // Notes on the sheet:
  //   s1
  //   s2
  //   s3
  //   s0
  //   s3
  //   s2
  //   s1
  //   s0
  //   B2 score
  //   B1 score
endmodule
