// Logisim project Control Unit.circ as structural Verilog: 1 circuit, main circuit main
module main (
  input  eq,
  input  gt,
  input  go,
  input  CLK,
  output Sa,
  output La,
  output Lb,
  output Sm,
  output Lm,
  output Lr,
  output Sadd,
  output [2:0] STATE
);

  wire and_1_out, and_2_out, and_3_out, and_4_out, and_5_out, and_6_out, and_7_out, and_8_out, not_1_out,
       not_2_out, not_3_out, not_4_out, not_5_out, not_6_out, not_7_out, not_8_out, not_9_out, not_10_out,
       not_11_out, not_12_out, not_13_out, not_14_out, not_15_out, not_16_out, not_17_out, not_18_out,
       not_19_out, not_20_out, not_21_out, not_22_out;
  wire [2:0] N0_out;

  Register #(.width(3)) u_STATE (.D(N0_out), .en(1'b1), .Q(STATE), .clk(CLK));  // open: clr
  not not_1 (not_1_out, STATE[2]);
  not not_2 (not_2_out, STATE[0]);
  not not_3 (not_3_out, STATE[2]);
  not not_4 (not_4_out, STATE[2]);
  not not_5 (not_5_out, STATE[1]);
  not not_6 (not_6_out, STATE[2]);
  not not_7 (not_7_out, STATE[0]);
  not not_8 (not_8_out, STATE[1]);
  not not_9 (not_9_out, STATE[0]);
  not not_10 (not_10_out, STATE[2]);
  not not_11 (not_11_out, STATE[1]);
  not not_12 (not_12_out, STATE[0]);
  not not_13 (not_13_out, STATE[2]);
  not not_14 (not_14_out, STATE[0]);
  not not_15 (not_15_out, STATE[2]);
  not not_16 (not_16_out, STATE[0]);
  and and_1 (and_1_out, not_1_out, STATE[1], not_2_out, eq);
  and and_2 (and_2_out, not_3_out, STATE[1], STATE[0]);
  and and_3 (and_3_out, not_4_out, not_5_out, STATE[0]);
  and and_4 (and_4_out, not_6_out, STATE[1], not_7_out, gt);
  and and_5 (and_5_out, STATE[2], not_8_out, not_9_out);
  and and_6 (and_6_out, not_10_out, not_11_out, not_12_out, go);
  and and_7 (and_7_out, not_13_out, STATE[1], not_14_out, gt);
  and and_8 (and_8_out, not_15_out, STATE[1], not_16_out, eq);
  or N2 (N0_out[2], and_1_out, and_2_out);
  or N1 (N0_out[1], and_3_out, and_4_out, and_5_out);
  or N0 (N0_out[0], and_6_out, and_7_out, and_8_out);
  not not_17 (not_17_out, STATE[2]);
  not not_18 (not_18_out, STATE[1]);
  and S1 (Lb, not_17_out, not_18_out, STATE[0]);
  not not_19 (not_19_out, STATE[2]);
  and S3 (Sadd, not_19_out, STATE[1], STATE[0]);
  and S4 (Sa, STATE[2], not_20_out, not_21_out);
  not not_20 (not_20_out, STATE[1]);
  not not_21 (not_21_out, STATE[0]);
  and S5 (Lr, STATE[2], not_22_out, STATE[0]);
  not not_22 (not_22_out, STATE[1]);
  or or_1 (La, Lb, Sa);
  or or_2 (Lm, Lb, Sadd, Lr);

  assign Sm = Sadd;

  // Notes on the sheet:
  //   P2
  //   P1
  //   P0
endmodule
