// Logisim project Datapath.circ as structural Verilog: 1 circuit, main circuit main
module main (
  input  [15:0] a_i,
  input  Sa,
  input  La,
  input  Lb,
  input  [15:0] b_i,
  input  Sm,
  input  Lm,
  input  Lr,
  input  Sadd,
  input  CLK,
  output gt,
  output eq,
  output lt,
  output [31:0] RESULT
);

  wire and_1_out, and_2_out, comparator_1_gt, comparator_1_lt, comparator_2_gt, comparator_2_lt, or_1_out;
  wire [15:0] a_q, b_q, bit_extender_4_out, multiplexer_1_out, multiplexer_2_out, multiplexer_3_out,
       negator_1_out, negator_2_out;
  wire [31:0] adder_1_out, bit_extender_1_out, bit_extender_2_out, bit_extender_3_out, demultiplexer_1_out0,
       demultiplexer_1_out1, mult_q, multiplexer_4_out, multiplexer_5_out, multiplexer_6_out, negator_3_out,
       result_reg_q;

  Comparator #(.width(16)) comparator_1 (
    .a(a_i), .b({16{1'b0}}), .gt(comparator_1_gt), .lt(comparator_1_lt));  // open: eq
  Comparator #(.width(16)) comparator_2 (
    .a(b_i), .b({16{1'b0}}), .gt(comparator_2_gt), .lt(comparator_2_lt));  // open: eq
  Negator #(.width(16)) negator_1 (.in(a_i), .out(negator_1_out));
  and and_1 (and_1_out, comparator_1_lt, comparator_2_gt);
  and and_2 (and_2_out, comparator_1_gt, comparator_2_lt);
  Multiplexer #(.width(16), .enable("false")) multiplexer_1 (
    .in0(a_i), .in1(negator_1_out), .out(multiplexer_1_out), .sel(comparator_1_lt));
  Multiplexer #(.width(16), .enable("false")) multiplexer_2 (
    .in0(b_i), .in1(negator_2_out), .out(multiplexer_2_out), .sel(comparator_2_lt));
  Negator #(.width(16)) negator_2 (.in(b_i), .out(negator_2_out));
  or or_1 (or_1_out, and_1_out, and_2_out);
  Multiplexer #(.width(16), .enable("false")) multiplexer_3 (
    .in0(multiplexer_1_out), .in1(bit_extender_4_out), .out(multiplexer_3_out), .sel(Sa));
  Register #(.width(16)) a (.D(multiplexer_3_out), .en(La), .Q(a_q), .clk(CLK));  // open: clr
  Register #(.width(16)) b (.D(multiplexer_2_out), .en(Lb), .Q(b_q), .clk(CLK));  // open: clr
  Multiplexer #(.width(32), .enable("false")) multiplexer_4 (
    .in0({32{1'b0}}), .in1(demultiplexer_1_out1), .out(multiplexer_4_out), .sel(Sm));
  assign bit_extender_1_out = {{16{1'b0}}, a_q};  // Bit_Extender bit_extender_1
  assign bit_extender_2_out = {{16{1'b0}}, b_q};  // Bit_Extender bit_extender_2
  Register #(.width(32)) mult (.D(multiplexer_4_out), .en(Lm), .Q(mult_q), .clk(CLK));  // open: clr
  Comparator #(.width(16)) comparator_3 (.a(a_q), .b({16{1'b0}}), .gt(gt), .eq(eq), .lt(lt));
  Register #(.width(32)) result_reg (.D(mult_q), .en(Lr), .Q(result_reg_q), .clk(CLK));  // open: clr
  assign bit_extender_3_out = {{31{1'b1}}, 1'b1};  // Bit_Extender bit_extender_3
  Multiplexer #(.width(32), .enable("false")) multiplexer_5 (
    .in0(bit_extender_1_out), .in1(bit_extender_2_out), .out(multiplexer_5_out), .sel(Sadd));
  Negator #(.width(32)) negator_3 (.in(result_reg_q), .out(negator_3_out));
  Multiplexer #(.width(32), .enable("false")) multiplexer_6 (
    .in0(bit_extender_3_out), .in1(mult_q), .out(multiplexer_6_out), .sel(Sadd));
  Multiplexer #(.width(32), .enable("false")) multiplexer_7 (
    .in0(result_reg_q), .in1(negator_3_out), .out(RESULT), .sel(or_1_out));
  Demultiplexer #(.width(32), .enable("false")) demultiplexer_1 (
    .out0(demultiplexer_1_out0), .out1(demultiplexer_1_out1), .in(adder_1_out), .sel(Sadd));
  Adder #(.width(32)) adder_1 (
    .a(multiplexer_5_out), .b(multiplexer_6_out), .out(adder_1_out), .cin(1'b0));  // open: cout
  Bit_Extender #(.in_width(32)) bit_extender_4 (.in(demultiplexer_1_out0), .out(bit_extender_4_out));
endmodule
