// Logisim project Main.circ as structural Verilog: 1 circuit, main circuit main
module main (
  input  [15:0] a_i,
  input  [15:0] b_i,
  output [2:0] state,
  output [31:0] RESULT
);

  wire clock_1_out, go_out, main_1_la, main_1_lb, main_1_lm, main_1_lr, main_1_sa, main_1_sadd, main_1_sm,
       main_2_eq, main_2_gt;

  Button go (.out(go_out));
  Clock clock_1 (.out(clock_1_out));
  control_unit_main main_1 (
    .eq(main_2_eq), .gt(main_2_gt), .go(go_out), .CLK(clock_1_out), .Sa(main_1_sa), .La(main_1_la),
    .Lb(main_1_lb), .Sm(main_1_sm), .Lm(main_1_lm), .Lr(main_1_lr), .Sadd(main_1_sadd), .STATE(state));
  datapath_main main_2 (
    .a_i(a_i), .Sa(main_1_sa), .La(main_1_la), .Lb(main_1_lb), .b_i(b_i), .Sm(main_1_sm), .Lm(main_1_lm),
    .Lr(main_1_lr), .Sadd(main_1_sadd), .CLK(clock_1_out), .gt(main_2_gt), .eq(main_2_eq), .RESULT(RESULT));  // open: lt
endmodule
