// Logisim project control unit.circ as structural Verilog: 1 circuit, main circuit main
module main (
  input  Start,
  input  Ceq,
  input  eq,
  input  Won,
  input  LedNum,
  input  AnyEq,
  input  CharInput,
  input  CLK,
  output Cw,
  output Rc,
  output Rloop,
  output Cwon,
  output Ltty,
  output Cled,
  output Lled,
  output NewLine,
  output [3:0] STATE
);

  wire and_1_out, and_2_out, and_3_out, and_4_out, and_5_out, and_6_out, and_7_out, and_8_out, and_9_out,
       and_10_out, and_11_out, and_12_out, and_13_out, and_14_out, and_15_out, and_16_out, and_17_out,
       and_18_out, and_19_out, and_20_out, and_21_out, and_22_out, and_23_out, and_24_out, and_25_out,
       and_26_out, and_27_out, and_28_out, and_29_out, and_30_out, and_31_out, and_32_out, and_33_out,
       S1_out, S3_out, S5_out, S11_out, S12_out, S13_out;
  wire [3:0] n0_out;

  Register #(.width(4)) register_1 (.D(n0_out), .en(1'b1), .Q(STATE), .clk(CLK));  // open: clr
  and and_1 (and_1_out, ~STATE[3], STATE[2], ~STATE[1], STATE[0], Ceq, ~eq);  // AND_Gate
  and and_2 (and_2_out, ~STATE[3], STATE[2], STATE[1], ~STATE[0], Won);  // AND_Gate
  and and_3 (and_3_out, STATE[3], ~STATE[2], ~STATE[1], ~STATE[0], LedNum);  // AND_Gate
  and and_4 (and_4_out, STATE[3], STATE[2], ~STATE[1], STATE[0], ~Start);  // AND_Gate
  and and_5 (and_5_out, STATE[3], ~STATE[2], STATE[1]);  // AND_Gate
  and and_6 (and_6_out, STATE[3], STATE[2], ~STATE[1], ~STATE[0]);  // AND_Gate
  and and_7 (and_7_out, ~STATE[3], STATE[2], ~STATE[1], ~STATE[0]);  // AND_Gate
  and and_8 (and_8_out, ~STATE[3], STATE[2], ~STATE[1], STATE[0], eq);  // AND_Gate
  and and_9 (and_9_out, ~STATE[3], STATE[2], ~STATE[1], STATE[0], ~Ceq, ~eq);  // AND_Gate
  and and_10 (and_10_out, STATE[3], ~STATE[2], ~STATE[1], ~STATE[0], ~LedNum);  // AND_Gate
  and and_11 (and_11_out, STATE[3], STATE[2], ~STATE[1], ~STATE[0], Ceq);  // AND_Gate
  and and_12 (and_12_out, STATE[3], STATE[2], ~STATE[1], STATE[0], ~Start);  // AND_Gate
  and and_13 (and_13_out, ~STATE[3], STATE[2], STATE[1], ~STATE[0], ~Won);  // AND_Gate
  and and_14 (and_14_out, STATE[3], ~STATE[2], STATE[0]);  // AND_Gate
  and and_15 (and_15_out, ~STATE[3], STATE[1], STATE[0]);  // AND_Gate
  and and_16 (and_16_out, ~STATE[3], ~STATE[2], ~STATE[1], STATE[0]);  // AND_Gate
  and and_17 (and_17_out, ~STATE[3], STATE[2], ~STATE[1], STATE[0], eq);  // AND_Gate
  and and_18 (and_18_out, ~STATE[3], STATE[2], ~STATE[1], STATE[0], ~Ceq, ~eq);  // AND_Gate
  and and_19 (and_19_out, ~STATE[3], STATE[2], STATE[1], ~STATE[0], Won);  // AND_Gate
  and and_20 (and_20_out, STATE[3], ~STATE[2], ~STATE[1], ~STATE[0], LedNum);  // AND_Gate
  and and_21 (and_21_out, STATE[3], ~STATE[2], STATE[1], ~STATE[0]);  // AND_Gate
  and and_22 (and_22_out, STATE[3], STATE[2], ~STATE[1], ~STATE[0], ~Ceq);  // AND_Gate
  and and_23 (and_23_out, ~STATE[3], ~STATE[2], ~STATE[1], ~STATE[0], Start);  // AND_Gate
  and and_24 (and_24_out, ~STATE[3], ~STATE[2], ~STATE[1], STATE[0], Ceq);  // AND_Gate
  and and_25 (and_25_out, ~STATE[3], ~STATE[2], STATE[1], ~STATE[0]);  // AND_Gate
  and and_26 (and_26_out, ~STATE[3], STATE[2], ~STATE[1], ~STATE[0], CharInput);  // AND_Gate
  and and_27 (and_27_out, ~STATE[3], STATE[2], ~STATE[1], STATE[0], ~Ceq, ~eq);  // AND_Gate
  and and_28 (and_28_out, ~STATE[3], STATE[2], ~STATE[1], STATE[0], Ceq, ~eq, AnyEq);  // AND_Gate
  and and_29 (and_29_out, ~STATE[3], STATE[2], STATE[1], ~STATE[0], ~Ceq, ~Won);  // AND_Gate
  and and_30 (and_30_out, ~STATE[3], STATE[2], STATE[1], STATE[0]);  // AND_Gate
  and and_31 (and_31_out, STATE[3], ~STATE[2], STATE[1], ~STATE[0]);  // AND_Gate
  and and_32 (and_32_out, STATE[3], STATE[2], ~STATE[1], ~STATE[0]);  // AND_Gate
  and and_33 (and_33_out, STATE[3], STATE[2], ~STATE[1], STATE[0], ~Start);  // AND_Gate
  or n3 (n0_out[3], and_1_out, and_2_out, and_3_out, and_4_out, and_5_out, and_6_out);
  or n2 (n0_out[2], and_7_out, and_8_out, and_9_out, and_10_out, and_11_out, and_12_out, and_13_out, and_14_out, and_15_out);
  or n1 (n0_out[1], and_16_out, and_17_out, and_18_out, and_19_out, and_20_out, and_21_out, and_22_out);
  or n0 (n0_out[0], and_23_out, and_24_out, and_25_out, and_26_out, and_27_out, and_28_out, and_29_out, and_30_out, and_31_out, and_32_out, and_33_out);
  and S1 (S1_out, ~STATE[3], ~STATE[2], ~STATE[1], STATE[0]);  // AND_Gate
  and S3 (S3_out, ~STATE[3], ~STATE[2], STATE[1], STATE[0]);  // AND_Gate
  and S4 (Rloop, ~STATE[3], STATE[2], ~STATE[1], ~STATE[0]);  // AND_Gate
  and S5 (S5_out, ~STATE[3], STATE[2], ~STATE[1], STATE[0]);  // AND_Gate
  and S6 (Cwon, ~STATE[3], STATE[2], STATE[1], ~STATE[0]);  // AND_Gate
  and S8 (Cled, STATE[3], ~STATE[2], ~STATE[1], ~STATE[0]);  // AND_Gate
  and S10 (NewLine, STATE[3], ~STATE[2], STATE[1], ~STATE[0]);  // AND_Gate
  and S11 (S11_out, STATE[3], ~STATE[2], STATE[1], STATE[0]);  // AND_Gate
  and S12 (S12_out, STATE[3], STATE[2], ~STATE[1], ~STATE[0]);  // AND_Gate
  and S13 (S13_out, STATE[3], STATE[2], ~STATE[1], STATE[0]);  // AND_Gate
  or S1_S5_S11 (Cw, S1_out, S5_out, S11_out);
  or S3_S4_S10_S13 (Rc, S3_out, Rloop, NewLine, S13_out);
  or S6_S12 (Ltty, Cwon, S13_out, S12_out);

  assign Lled = Cled;

  // Notes on the sheet:
  //   Start Ceq eq Won Lednum AnyEq CharInput
endmodule
