// Logisim project datapath.circ as structural Verilog: 1 circuit, main circuit main
module main (
  input  [7:0] _0,
  input  [7:0] _1,
  input  [7:0] _2,
  input  [7:0] _3,
  input  [7:0] _4,
  input  NewLine,
  input  [7:0] _5,
  input  Ltty,
  input  [7:0] _6,
  input  [7:0] _7,
  input  Cw,
  input  Rc,
  input  a,
  input  b,
  input  c,
  input  d,
  input  e,
  input  f,
  input  g,
  input  h,
  input  i,
  input  j,
  input  k,
  input  l,
  input  m,
  input  n,
  input  o,
  input  p,
  input  q,
  input  r,
  input  s,
  input  t,
  input  u,
  input  v,
  input  w,
  input  x,
  input  y,
  input  z,
  input  Cwon,
  input  Cled,
  input  Rloop,
  input  Lled,
  input  clk,
  input  Start,
  output [3:0] NumOfChar,
  output Ceq,
  output eq,
  output won,
  output LedNum,
  output Led1,
  output Led2,
  output Led3,
  output Led4,
  output Led5,
  output Led6,
  output Led7,
  output Led8,
  output Led9,
  output Led10,
  output AnyEq,
  output CharInput
);

  wire and_1_out, comparator_2_eq, comparator_5_eq, comparator_8_eq, comparator_9_eq, comparator_10_eq,
       comparator_11_eq, comparator_12_eq, comparator_13_eq, comparator_14_eq, comparator_15_eq,
       comparator_16_eq, comparator_17_eq, counter_2_q, not_1_out, not_2_out, or_1_out;
  wire [2:0] bit_extender_3_out, counter_1_q;
  wire [3:0] bit_extender_2_out, counter_3_q, counter_5_q, subtractor_1_out, subtractor_2_out;
  wire [6:0] bit_extender_1_out, multiplexer_22_out, register_1_q;
  wire [7:0] counter_4_q, multiplexer_1_out, multiplexer_15_out, register_2_q;

  Multiplexer #(.width(8), .enable("false")) multiplexer_1 (
    .in1(8'h61), .out(multiplexer_1_out), .sel(a));  // open: in0
  Multiplexer #(.width(8), .enable("false")) multiplexer_2 (
    .in1(8'h6e), .out(multiplexer_1_out), .sel(n));  // open: in0
  Multiplexer #(.width(8), .enable("false")) multiplexer_3 (
    .in1(8'h62), .out(multiplexer_1_out), .sel(b));  // open: in0
  Multiplexer #(.width(8), .enable("false")) multiplexer_4 (
    .in1(8'h6f), .out(multiplexer_1_out), .sel(o));  // open: in0
  Multiplexer #(.width(8), .enable("false")) multiplexer_5 (
    .in1(8'h63), .out(multiplexer_1_out), .sel(c));  // open: in0
  Multiplexer #(.width(8), .enable("false")) multiplexer_6 (
    .in1(8'h64), .out(multiplexer_1_out), .sel(d));  // open: in0
  Multiplexer #(.width(8), .enable("false")) multiplexer_7 (
    .in1(8'h70), .out(multiplexer_1_out), .sel(p));  // open: in0
  Multiplexer #(.width(8), .enable("false")) multiplexer_8 (
    .in1(8'h71), .out(multiplexer_1_out), .sel(q));  // open: in0
  Multiplexer #(.width(8), .enable("false")) multiplexer_9 (
    .in1(8'h65), .out(multiplexer_1_out), .sel(e));  // open: in0
  Multiplexer #(.width(8), .enable("false")) multiplexer_10 (
    .in1(8'h72), .out(multiplexer_1_out), .sel(r));  // open: in0
  Multiplexer #(.width(8), .enable("false")) multiplexer_11 (
    .in1(8'h73), .out(multiplexer_1_out), .sel(s));  // open: in0
  Multiplexer #(.width(8), .enable("false")) multiplexer_12 (
    .in1(8'h67), .out(multiplexer_1_out), .sel(g));  // open: in0
  Multiplexer #(.width(8), .enable("false")) multiplexer_13 (
    .in1(8'h66), .out(multiplexer_1_out), .sel(f));  // open: in0
  Multiplexer #(.width(8), .enable("false")) multiplexer_14 (
    .in1(8'h74), .out(multiplexer_1_out), .sel(t));  // open: in0
  Multiplexer #(.select(3), .width(8), .enable("false")) multiplexer_15 (
    .in0(_0), .in1(_1), .in2(_2), .in3(_3), .in4(_4), .in5(_5), .in6(_6), .in7(_7), .out(multiplexer_15_out),
    .sel(counter_1_q));
  Counter #(.width(3), .max('h7)) counter_1 (
    .D(bit_extender_3_out), .Q(counter_1_q), .clk(Cw), .clr(Rc));  // open: load, count, carry
  Multiplexer #(.width(8), .enable("false")) multiplexer_16 (
    .in1(8'h69), .out(multiplexer_1_out), .sel(i));  // open: in0
  Multiplexer #(.width(8), .enable("false")) multiplexer_17 (
    .in1(8'h68), .out(multiplexer_1_out), .sel(h));  // open: in0
  Multiplexer #(.width(8), .enable("false")) multiplexer_18 (
    .in1(8'h75), .out(multiplexer_1_out), .sel(u));  // open: in0
  Multiplexer #(.width(8), .enable("false")) multiplexer_19 (
    .in1(8'h76), .out(multiplexer_1_out), .sel(v));  // open: in0
  Bit_Extender #(.out_width(7)) bit_extender_1 (.in(multiplexer_15_out), .out(bit_extender_1_out));
  Multiplexer #(.width(8), .enable("false")) multiplexer_20 (
    .in1(8'h6a), .out(multiplexer_1_out), .sel(j));  // open: in0
  Multiplexer #(.width(8), .enable("false")) multiplexer_21 (
    .in1(8'h77), .out(multiplexer_1_out), .sel(w));  // open: in0
  Multiplexer #(.width(7), .enable("false")) multiplexer_22 (
    .in0(bit_extender_1_out), .in1(7'b0001010), .out(multiplexer_22_out), .sel(NewLine));
  Comparator #(.width(3)) comparator_1 (.a(counter_1_q), .b(3'b111), .eq(Ceq));  // open: gt, lt
  Multiplexer #(.width(8), .enable("false")) multiplexer_23 (
    .in1(8'h6b), .out(multiplexer_1_out), .sel(k));  // open: in0
  Multiplexer #(.width(8), .enable("false")) multiplexer_24 (
    .in1(8'h6c), .out(multiplexer_1_out), .sel(l));  // open: in0
  Multiplexer #(.width(8), .enable("false")) multiplexer_25 (
    .in1(8'h79), .out(multiplexer_1_out), .sel(y));  // open: in0
  Multiplexer #(.width(8), .enable("false")) multiplexer_26 (
    .in1(8'h78), .out(multiplexer_1_out), .sel(x));  // open: in0
  Register #(.width(7)) register_1 (.D(multiplexer_22_out), .en(Ltty), .Q(register_1_q), .clk(Ltty), .clr(Start));
  Multiplexer #(.width(8), .enable("false")) multiplexer_27 (
    .in1(8'h6d), .out(multiplexer_1_out), .sel(m));  // open: in0
  Multiplexer #(.width(8), .enable("false")) multiplexer_28 (
    .in1(8'h7a), .out(multiplexer_1_out), .sel(z));  // open: in0
  or or_1 (or_1_out, m, l, k, i, v, u, s, e, r, q, p, o, a, n, b, c, d, f, t, g, h, w, j, x, y, z);
  TTY #(.rows(4), .cols(26)) tty_1 (.data(register_1_q), .clk(Ltty), .clr(Start));  // open: we
  Counter #(.width(1), .max('h1)) counter_2 (
    .load(or_1_out), .D(1'b1), .count(1'b0), .Q(counter_2_q), .clk(or_1_out), .clr(Start));  // open: carry
  Comparator comparator_2 (.a({8{1'b0}}), .b(multiplexer_1_out), .eq(comparator_2_eq));  // open: gt, lt
  Multiplexer #(.width(8), .enable("false")) multiplexer_29 (
    .in1({8{1'b0}}), .out(multiplexer_1_out), .sel(not_1_out));  // open: in0
  not not_1 (not_1_out, or_1_out);
  assign bit_extender_2_out = {{1{1'b0}}, counter_1_q};  // Bit_Extender bit_extender_2
  Register register_2 (.D(multiplexer_1_out), .en(counter_2_q), .Q(register_2_q), .clk(counter_2_q), .clr(Start));
  and and_1 (and_1_out, ~comparator_2_eq, eq);  // AND_Gate
  Comparator #(.width(1)) comparator_3 (.a(not_1_out), .b(1'b0), .eq(CharInput));  // open: gt, lt
  Subtractor #(.width(4)) subtractor_1 (
    .a(4'b1000), .b(bit_extender_2_out), .out(subtractor_1_out));  // open: bin, bout
  Comparator comparator_4 (.a(multiplexer_15_out), .b(register_2_q), .eq(eq));  // open: gt, lt
  Register #(.width(1)) register_3 (.D(and_1_out), .en(and_1_out), .Q(AnyEq), .clk(clk), .clr(Rloop));
  Register #(.width(4)) register_4 (.D(subtractor_1_out), .en(not_2_out), .Q(NumOfChar), .clk(not_2_out), .clr(Start));
  Subtractor #(.width(4)) subtractor_2 (.a(4'b1000), .b(NumOfChar), .out(subtractor_2_out));  // open: bin, bout
  Counter #(.width(4), .max('hf)) counter_3 (.Q(counter_3_q), .clk(Cwon), .clr(Start));  // open: load, D, count, carry
  Counter counter_4 (.Q(counter_4_q), .clk(Cled), .clr(Start));  // open: load, D, count, carry
  Counter #(.width(4), .max('hf)) counter_5 (
    .count(Lled), .Q(counter_5_q), .clk(Lled), .clr(Start));  // open: load, D, carry
  not not_2 (not_2_out, comparator_5_eq);
  Comparator comparator_5 (.a(multiplexer_15_out), .b({8{1'b0}}), .eq(comparator_5_eq));  // open: gt, lt
  Bit_Extender #(.in_width(4), .out_width(3)) bit_extender_3 (.in(subtractor_2_out), .out(bit_extender_3_out));
  Comparator #(.width(4)) comparator_6 (.a(NumOfChar), .b(counter_3_q), .eq(won));  // open: gt, lt
  Comparator comparator_7 (.a(8'ha), .b(counter_4_q), .eq(LedNum));  // open: gt, lt
  Comparator #(.width(4)) comparator_8 (.a(4'b0001), .b(counter_5_q), .eq(comparator_8_eq));  // open: gt, lt
  Comparator #(.width(4)) comparator_9 (.a(4'b0010), .b(counter_5_q), .eq(comparator_9_eq));  // open: gt, lt
  Comparator #(.width(4)) comparator_10 (.a(4'b0011), .b(counter_5_q), .eq(comparator_10_eq));  // open: gt, lt
  Comparator #(.width(4)) comparator_11 (.a(4'b0100), .b(counter_5_q), .eq(comparator_11_eq));  // open: gt, lt
  Comparator #(.width(4)) comparator_12 (.a(4'b0101), .b(counter_5_q), .eq(comparator_12_eq));  // open: gt, lt
  Comparator #(.width(4)) comparator_13 (.a(4'b0110), .b(counter_5_q), .eq(comparator_13_eq));  // open: gt, lt
  Comparator #(.width(4)) comparator_14 (.a(4'b0111), .b(counter_5_q), .eq(comparator_14_eq));  // open: gt, lt
  Comparator #(.width(4)) comparator_15 (.a(4'b1000), .b(counter_5_q), .eq(comparator_15_eq));  // open: gt, lt
  Comparator #(.width(4)) comparator_16 (.a(4'b1001), .b(counter_5_q), .eq(comparator_16_eq));  // open: gt, lt
  Comparator #(.width(4)) comparator_17 (.a(4'b1010), .b(counter_5_q), .eq(comparator_17_eq));  // open: gt, lt
  Register #(.width(1)) register_5 (.D(comparator_8_eq), .en(comparator_8_eq), .Q(Led1), .clk(clk), .clr(Start));
  Register #(.width(1)) register_6 (.D(comparator_9_eq), .en(comparator_9_eq), .Q(Led2), .clk(clk), .clr(Start));
  Register #(.width(1)) register_7 (.D(comparator_10_eq), .en(comparator_10_eq), .Q(Led3), .clk(clk), .clr(Start));
  Register #(.width(1)) register_8 (.D(comparator_11_eq), .en(comparator_11_eq), .Q(Led4), .clk(clk), .clr(Start));
  Register #(.width(1)) register_9 (.D(comparator_12_eq), .en(comparator_12_eq), .Q(Led5), .clk(clk), .clr(Start));
  Register #(.width(1)) register_10 (.D(comparator_13_eq), .en(comparator_13_eq), .Q(Led6), .clk(clk), .clr(Start));
  Register #(.width(1)) register_11 (.D(comparator_14_eq), .en(comparator_14_eq), .Q(Led7), .clk(clk), .clr(Start));
  Register #(.width(1)) register_12 (.D(comparator_15_eq), .en(comparator_15_eq), .Q(Led8), .clk(clk), .clr(Start));
  Register #(.width(1)) register_13 (.D(comparator_16_eq), .en(comparator_16_eq), .Q(Led9), .clk(clk), .clr(Start));
  Register #(.width(1)) register_14 (.D(comparator_17_eq), .en(comparator_17_eq), .Q(Led10), .clk(clk), .clr(Start));
endmodule
