// Logisim project main.circ as structural Verilog: 1 circuit, main circuit main
module main (
  input  [7:0] _0,
  input  [7:0] _1,
  input  [7:0] _2,
  input  [7:0] _3,
  input  [7:0] _4,
  input  [7:0] _5,
  input  [7:0] _6,
  input  [7:0] _7,
  output [3:0] STATE
);

  wire a_out, b_out, c_out, CLK_out, d_out, e_out, f_out, g_out, h_out, i_out, j_out, k_out, l_out, m_out,
       main_1_da, main_1_db, main_1_dc, main_1_dd, main_1_de, main_1_df, main_1_dg, main_2_anyeq, main_2_ceq,
       main_2_charinput, main_2_eq, main_2_led1, main_2_led2, main_2_led3, main_2_led4, main_2_led5,
       main_2_led6, main_2_led7, main_2_led8, main_2_led9, main_2_led10, main_2_lednum, main_2_won,
       main_3_cled, main_3_cw, main_3_cwon, main_3_lled, main_3_ltty, main_3_newline, main_3_rc,
       main_3_rloop, n_out, o_out, p_out, q_out, r_out, s_out, START_out, t_out, u_out, v_out, w_out, x_out,
       y_out, z_out;
  wire [3:0] main_2_numofchar;

  _7_Segment_Display_main main_1 (
    .ABCD(main_2_numofchar), .DA(main_1_da), .DB(main_1_db), .DC(main_1_dc), .DD(main_1_dd), .DE(main_1_de),
    .DF(main_1_df), .DG(main_1_dg));
  Button START (.out(START_out));
  Clock CLK (.out(CLK_out));
  _7_Segment_Display u_7_segment_display_1 (
    .g(main_1_dg), .f(main_1_df), .a(main_1_da), .b(main_1_db), .e(main_1_de), .d(main_1_dd), .c(main_1_dc));  // open: dp
  Button a (.out(a_out));
  Button n (.out(n_out));
  Button c (.out(c_out));
  Button b (.out(b_out));
  Button o (.out(o_out));
  Button d (.out(d_out));
  Button p (.out(p_out));
  Button q (.out(q_out));
  Button f (.out(f_out));
  Button e (.out(e_out));
  Button s (.out(s_out));
  Button r (.out(r_out));
  Button g (.out(g_out));
  Button h (.out(h_out));
  Button t (.out(t_out));
  Button i (.out(i_out));
  Button v (.out(v_out));
  Button u (.out(u_out));
  Button j (.out(j_out));
  Button k (.out(k_out));
  Button w (.out(w_out));
  datapath_main main_2 (
    ._0(_0), ._1(_1), ._2(_2), ._3(_3), ._4(_4), ._5(_5), .Ltty(main_3_ltty), ._6(_6), ._7(_7),
    .Cw(main_3_cw), .Cwon(main_3_cwon), .Cled(main_3_cled), .Lled(main_3_lled), .clk(CLK_out),
    .Start(START_out), .n(n_out), .a(a_out), .o(o_out), .b(b_out), .p(p_out), .c(c_out), .q(q_out),
    .d(d_out), .r(r_out), .e(e_out), .s(s_out), .f(f_out), .t(t_out), .g(g_out), .u(u_out), .h(h_out),
    .v(v_out), .i(i_out), .w(w_out), .j(j_out), .x(x_out), .k(k_out), .y(y_out), .l(l_out), .z(z_out),
    .m(m_out), .Led1(main_2_led1), .Led2(main_2_led2), .Led3(main_2_led3), .Led4(main_2_led4),
    .Led5(main_2_led5), .Led6(main_2_led6), .Led7(main_2_led7), .Led8(main_2_led8), .Led9(main_2_led9),
    .Led10(main_2_led10), .Rc(main_3_rc), .NewLine(main_3_newline), .Rloop(main_3_rloop),
    .NumOfChar(main_2_numofchar), .Ceq(main_2_ceq), .eq(main_2_eq), .won(main_2_won), .LedNum(main_2_lednum),
    .AnyEq(main_2_anyeq), .CharInput(main_2_charinput));
  Button l (.out(l_out));
  Button y (.out(y_out));
  Button x (.out(x_out));
  Button m (.out(m_out));
  Button z (.out(z_out));
  LED WON (.in(main_2_won));
  LED led_1 (.in(main_2_led1));
  LED led_2 (.in(main_2_led2));
  LED led_3 (.in(main_2_led3));
  LED led_4 (.in(main_2_led4));
  LED led_5 (.in(main_2_led5));
  LED led_6 (.in(main_2_led6));
  LED led_7 (.in(main_2_led7));
  LED led_8 (.in(main_2_led8));
  LED led_9 (.in(main_2_led9));
  LED led_10 (.in(main_2_led10));
  control_unit_main main_3 (
    .Start(START_out), .Ceq(main_2_ceq), .eq(main_2_eq), .Won(main_2_won), .LedNum(main_2_lednum),
    .AnyEq(main_2_anyeq), .CharInput(main_2_charinput), .CLK(CLK_out), .Cw(main_3_cw), .Rc(main_3_rc),
    .Rloop(main_3_rloop), .Cwon(main_3_cwon), .Ltty(main_3_ltty), .Cled(main_3_cled), .Lled(main_3_lled),
    .NewLine(main_3_newline), .STATE(STATE));
  LED LOST (.in(main_2_led10));

  // Notes on the sheet:
  //   h->01101000
  //   e->01100101
  //   l->01101100
  //   l->01101100
  //   o->01101111
  //   Number of Characters
endmodule
